# Fritzing sketch ioe2_p2 (saved by Fritzing 0.9.2b)
breadboards: 1

parts:
  Part3 = Adafruit Feather HUZZAH ESP8266 [part_number="Adafruit #2821"]
  LED1 = LED - 5mm [color="Blue (430nm)" package="5 mm [THT]"]
  LED2 = LED - 5mm [color="White (8000K)" package="5 mm [THT]"]
  R1 = Resistor [tolerance=±5% resistance=220 package=THT]
  R2 = Resistor [tolerance=±5% resistance=1k package=THT]
  S5 = Round Pushbutton
  U1 = SWITCH-SPST-2 [package=switch-spst-vertical]

nets:
  N1: Part3.GND, LED1.anode, LED2.anode, S5.leg1, U1.P
  N2: Part3.3.3V, R1.Pin_1, R2.Pin_0
  N3: Part3.GPIO15, R2.Pin_1, S5.leg0
  N4: R1.Pin_0, U1.O

custom parts:
  Adafruit Feather HUZZAH ESP8266: his is the Adafruit Feather HUZZAH ESP8266 - our take on an 'all-in-one' ESP8266 WiFi development board with built in USB and battery charging. Its an ESP8266 WiFi module with all the extras you need, ready to rock! We have other boards in the Feather family, check'em out here. At the Feather HUZZAH's heart is an ESP8266 WiFi microcontroller clocked at 80 MHz and at 3.3V logic. This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
